# Fritzing sketch prjet_electro_1 (saved by Fritzing 0.9.3b)
breadboards: 1

parts:
  Composant3 = Arduino Uno (Rev3)
  X2 = X113647 Stepper Driver Board [package=board]
  MOTOR2 = 28BYJ-48 Stepper Motor
  R3 = Resistor [tolerance=±5% resistance=220 package=THT]
  R4 = Resistor [tolerance=±5% resistance=220 package=THT]
  LED5 = LED - 5mm [color="Red (633nm)" package="5 mm [THT]"]
  LED6 = LED - 5mm [color="Green (560nm)" package="5 mm [THT]"]
  LCM1602_IIC2 = LCM1602 IIC [part_number="LCM1602 IIC" chip_label="LCM1602 IIC" package="DIP (Dual Inline) [THT]"]
  LCD2 = LCD screen
  Keypad4x2 = Keypad Membran 4x4
  5V_Input = Power plug
  R5 = Rotary Potentiometer (Small) [maximum_resistance=100kΩ package=THT]
  U2 = ESP8266 WiFi Module [part_number=ESP8266]
  Composant4 = RFID-RC522-v2
  X3 = X113647 Stepper Driver Board [package=board]  # not connected

nets:
  N1: Composant3.A0, R5.wiper
  N2: Composant3.A4/SDA, LCM1602_IIC2.SDA, Keypad4x2.Pin8
  N3: Composant3.A5/SCL, LCM1602_IIC2.SCL
  N4: Composant3.D8, Keypad4x2.Pin3
  N5: Composant3.D9_PWM, Keypad4x2.Pin4, Composant4.RST
  N6: Composant3.D10_PWM/SS, R3.Pin_0, Composant4.SDA
  N7: Composant3.D11_PWM/MOSI, Composant4.MOSI
  N8: Composant3.D12/MISO, Composant4.MISO
  N9: Composant3.D13/SCK, R4.Pin_0, Composant4.SCK
  N10: Composant3.D0/RX, U2.RXD
  N11: Composant3.D1/TX, U2.TXD
  N12: Composant3.D2, X2.IN1
  N13: Composant3.D3_PWM, X2.IN2
  N14: Composant3.D4, X2.IN3
  N15: Composant3.D6_PWM, Keypad4x2.Pin1
  N16: Composant3.D7, Keypad4x2.Pin2
  VCC: Composant3.3V3, LCM1602_IIC2.VCC, R5.leg1, U2.VCC, U2.CH_PD, Composant4.3_3V
  GND: Composant3.GND, X2.GND, LED5.cathode, LED6.cathode, LCM1602_IIC2.GND, 5V_Input.GND, R5.leg2, U2.GPIO_0, U2.GND, Composant4.GND
  N17: X2.+V, 5V_Input.VCC
  N18: X2.BLUE, MOTOR2.BLUE
  N19: X2.PINK, MOTOR2.PINK
  N20: X2.YELLOW, MOTOR2.YELLOW
  N21: X2.ORANGE, MOTOR2.ORANGE
  N22: X2.RED, MOTOR2.RED
  VSS: LCM1602_IIC2.VSS, LCD2.VSS
  VDD: LCM1602_IIC2.VDD, LCD2.VDD
  N23: LCM1602_IIC2.V0, LCD2.V0
  N24: LCM1602_IIC2.RS, LCD2.RS
  N25: LCM1602_IIC2.RW, LCD2.R/W
  N26: LCM1602_IIC2.E, LCD2.E
  N27: LCM1602_IIC2.D0, LCD2.DB0
  N28: LCM1602_IIC2.D1, LCD2.DB1
  N29: LCM1602_IIC2.D2, LCD2.DB2
  N30: LCM1602_IIC2.D3, LCD2.DB3
  N31: LCM1602_IIC2.D4, LCD2.DB4
  N32: LCM1602_IIC2.D5, LCD2.DB5
  N33: LCM1602_IIC2.D6, LCD2.DB6
  N34: LCM1602_IIC2.D7, LCD2.DB7
  N35: LCM1602_IIC2.A, LCD2.LED+
  N36: LCM1602_IIC2.K, LCD2.LED-
  N37: LCM1602_IIC2.LED_A, LCM1602_IIC2.LED_B

custom parts:
  X113647 Stepper Driver Board: A common stepper motor driver board based on ULN2003APG darlington array
  28BYJ-48 Stepper Motor: 28BYJ-48 gear-reduction stepper motor (small)
  LCM1602 IIC: I2C-Module to use a 1602 or 2004 LCD on with the wire.h libory Serial LCD Modul
  Keypad Membran 4x4: Membrane Keypad 4x4 Matrix
  ESP8266 WiFi Module: Generic WiFi Module based on the ESP8266 with onboard PCB antenna and UART communications
  RFID-RC522-v2: A simple China made RFID-RC522 Reader; do check the pin labels, as this is a MFRC522 based clone.
