# Fritzing sketch prjet_electro_1_latest_update_sans_alimentation (saved by Fritzing 0.9.3b)
breadboards: 1

parts:
  Composant2 = RFID USB Reader
  U1 = ESP8266 WiFi Module [part_number=ESP8266]
  Composant3 = Arduino Uno (Rev3)
  X2 = X113647 Stepper Driver Board [package=board]
  MOTOR2 = 28BYJ-48 Stepper Motor
  R3 = Resistor [tolerance=±5% resistance=220 package=THT]
  R4 = Resistor [tolerance=±5% resistance=220 package=THT]
  LED5 = LED - 5mm [color="Red (633nm)" package="5 mm [THT]"]
  LED6 = LED - 5mm [color="Green (560nm)" package="5 mm [THT]"]
  LCM1602_IIC2 = LCM1602 IIC [part_number="LCM1602 IIC" chip_label="LCM1602 IIC" package="DIP (Dual Inline) [THT]"]
  LCD2 = LCD screen
  Keypad4x2 = Keypad Membran 4x4

nets:
  GND: Composant2.CP, Composant2.GND, U1.GND, U1.GPIO_16, U1.REST, Composant3.GND, X2.GND, LED5.cathode, LED6.cathode, LCM1602_IIC2.GND
  N1: Composant2.ANT2, Composant3.A4/SDA, LCM1602_IIC2.SDA, Keypad4x2.Pin8
  N2: Composant2.ANT1, Composant3.D11_PWM/MOSI
  N3: Composant2.TX-O-RS232, Composant3.D12/MISO
  N4: Composant2.TX-O, Composant3.D13/SCK, R4.Pin_0
  VCC: Composant2.VCC, U1.VCC, U1.CH_PD, Composant3.3V3, X2.+V, LCM1602_IIC2.VCC
  N5: U1.RXD, Composant3.D0/RX
  N6: U1.TXD, Composant3.D1/TX
  N7: Composant3.A5/SCL, LCM1602_IIC2.SCL
  N8: Composant3.D8, Keypad4x2.Pin3
  N9: Composant3.D9_PWM, Keypad4x2.Pin4
  N10: Composant3.D10_PWM/SS, R3.Pin_0
  N11: Composant3.D2, X2.IN1
  N12: Composant3.D3_PWM, X2.IN2
  N13: Composant3.D5_PWM, X2.IN3
  N14: Composant3.D6_PWM, Keypad4x2.Pin1
  N15: Composant3.D7, Keypad4x2.Pin2
  N16: X2.BLUE, MOTOR2.BLUE
  N17: X2.PINK, MOTOR2.PINK
  N18: X2.YELLOW, MOTOR2.YELLOW
  N19: X2.ORANGE, MOTOR2.ORANGE
  N20: X2.RED, MOTOR2.RED
  VSS: LCM1602_IIC2.VSS, LCD2.VSS
  VDD: LCM1602_IIC2.VDD, LCD2.VDD
  N21: LCM1602_IIC2.V0, LCD2.V0
  N22: LCM1602_IIC2.RS, LCD2.RS
  N23: LCM1602_IIC2.RW, LCD2.R/W
  N24: LCM1602_IIC2.E, LCD2.E
  N25: LCM1602_IIC2.D0, LCD2.DB0
  N26: LCM1602_IIC2.D1, LCD2.DB1
  N27: LCM1602_IIC2.D2, LCD2.DB2
  N28: LCM1602_IIC2.D3, LCD2.DB3
  N29: LCM1602_IIC2.D4, LCD2.DB4
  N30: LCM1602_IIC2.D5, LCD2.DB5
  N31: LCM1602_IIC2.D6, LCD2.DB6
  N32: LCM1602_IIC2.D7, LCD2.DB7
  N33: LCM1602_IIC2.A, LCD2.LED+
  N34: LCM1602_IIC2.K, LCD2.LED-
  N35: LCM1602_IIC2.LED_A, LCM1602_IIC2.LED_B

custom parts:
  X113647 Stepper Driver Board: A common stepper motor driver board based on ULN2003APG darlington array
  28BYJ-48 Stepper Motor: 28BYJ-48 gear-reduction stepper motor (small)
  LCM1602 IIC: I2C-Module to use a 1602 or 2004 LCD on with the wire.h libory Serial LCD Modul
  Keypad Membran 4x4: Membrane Keypad 4x4 Matrix
