# Fritzing sketch projetElectronique_1 (saved by Fritzing 0.9.3b)
breadboards: 1

parts:
  Composant1 = Arduino Uno (Rev3)
  Keypad4x1 = Keypad Membran 4x4
  LCM1602_IIC1 = LCM1602 IIC [part_number="LCM1602 IIC" chip_label="LCM1602 IIC" package="DIP (Dual Inline) [THT]"]
  LCD1 = LCD screen
  R1 = Resistor [tolerance=±5% resistance=220 package=THT]
  R2 = Resistor [tolerance=±5% resistance=220 package=THT]
  LED3 = LED - 5mm [color="Red (633nm)" package="5 mm [THT]"]
  LED4 = LED - 5mm [color="Green (560nm)" package="5 mm [THT]"]
  X1 = X113647 Stepper Driver Board [package=board]
  MOTOR1 = 28BYJ-48 Stepper Motor

nets:
  N1: Composant1.A1, Keypad4x1.Pin5
  N2: Composant1.A2, Keypad4x1.Pin6
  N3: Composant1.A3, Keypad4x1.Pin7
  N4: Composant1.A4/SDA, Keypad4x1.Pin8, LCM1602_IIC1.SDA
  N5: Composant1.A5/SCL, LCM1602_IIC1.SCL
  N6: Composant1.D8, Keypad4x1.Pin3
  N7: Composant1.D9_PWM, Keypad4x1.Pin4
  N8: Composant1.D10_PWM/SS, R2.Pin_0
  N9: Composant1.D13/SCK, R1.Pin_0
  N10: Composant1.D2, X1.IN1
  N11: Composant1.D3_PWM, X1.IN2
  N12: Composant1.D5_PWM, X1.IN3
  N13: Composant1.D6_PWM, Keypad4x1.Pin1
  N14: Composant1.D7, Keypad4x1.Pin2
  5V: Composant1.5V, LCM1602_IIC1.VCC, X1.+V
  GND: Composant1.GND, LCM1602_IIC1.GND, LED3.cathode, LED4.cathode, X1.GND
  VSS: LCM1602_IIC1.VSS, LCD1.VSS
  VDD: LCM1602_IIC1.VDD, LCD1.VDD
  N15: LCM1602_IIC1.V0, LCD1.V0
  N16: LCM1602_IIC1.RS, LCD1.RS
  N17: LCM1602_IIC1.RW, LCD1.R/W
  N18: LCM1602_IIC1.E, LCD1.E
  N19: LCM1602_IIC1.D0, LCD1.DB0
  N20: LCM1602_IIC1.D1, LCD1.DB1
  N21: LCM1602_IIC1.D2, LCD1.DB2
  N22: LCM1602_IIC1.D3, LCD1.DB3
  N23: LCM1602_IIC1.D4, LCD1.DB4
  N24: LCM1602_IIC1.D5, LCD1.DB5
  N25: LCM1602_IIC1.D6, LCD1.DB6
  N26: LCM1602_IIC1.D7, LCD1.DB7
  N27: LCM1602_IIC1.A, LCD1.LED+
  N28: LCM1602_IIC1.K, LCD1.LED-
  N29: LCM1602_IIC1.LED_A, LCM1602_IIC1.LED_B
  N30: X1.BLUE, MOTOR1.BLUE
  N31: X1.PINK, MOTOR1.PINK
  N32: X1.YELLOW, MOTOR1.YELLOW
  N33: X1.ORANGE, MOTOR1.ORANGE
  N34: X1.RED, MOTOR1.RED

custom parts:
  Keypad Membran 4x4: Membrane Keypad 4x4 Matrix
  LCM1602 IIC: I2C-Module to use a 1602 or 2004 LCD on with the wire.h libory Serial LCD Modul
  X113647 Stepper Driver Board: A common stepper motor driver board based on ULN2003APG darlington array
  28BYJ-48 Stepper Motor: 28BYJ-48 gear-reduction stepper motor (small)

// code stored in the sketch: Untitled.ino
//importation de la librairie pour LCD
#include <LiquidCrystal.h>
//importation du clavier numerique
#include <Keypad.h>
//importation je ne sais quoi
#include <EEPROM.h>
// definition de la constante pour le mot de passe
#define Password_Lenght 5

//declaration des ports du LCD sur les broches de l'arduino
const int rs = 12, en = 11, d4 = 5, d5 = 4, d6 = 3, d7 = 2;
//initialisation de l'afficheur avec les ports
LiquidCrystal lcd(rs, en, d4, d5, d6, d7);

//nombre de ligne du keypad
const byte ROWS = 4; 
//nombre de colonne du keypad
const byte COLS = 4; 
//representation du keypad
char keys[ROWS][COLS] = {
  {'1','2','3','A'},
  {'4','5','6','B'},
  {'7','8','9','C'},
  {'*','0','#','D'}
};
//activation des broches pour les lignes
byte rowPins[ROWS] = {6, 7, 8, 9}; 
//activation des broches pour les colonnes
byte colPins[COLS] = {A1, A2, A3, A4}; 

char Data[Password_Lenght]; 
char Data2[Password_Lenght];
char Master[Password_Lenght];
byte data_count = 0, master_count = 0;
bool Pass_is_good;
char key;
byte key_state = 0;
char last_press_key;
byte mode = 0;

int change_password_allow_time = 10000;
long time_old = 0;
bool just_allowed_pass =0;

char FistTimePassword[] = {'1','2','3','4'}; // setup first-time password here


Keypad keypad = Keypad( makeKeymap(keys), rowPins, colPins, ROWS, COLS );

void setup(){
  Serial.begin(9600);
  Check_EEPROM();

  lcd.begin(16, 2);

  pinMode(13, OUTPUT);
  digitalWrite(13, LOW);
  
}
  
void loop()
{
  key = keypad.getKey(); 
  key_state = keypad.getState();

  if(key){
    last_press_key = key;
    Serial.println(key);
  }


if( mode == 3){
    if(last_press_key == '#' && key_state == 2){
      mode = 1;
    }
    if(last_press_key == '*' && key_state == 2){
      mode = 0;
    lcd.clear();
    lcd.setCursor(4,0);
    lcd.print("LOCKED");
    digitalWrite(13, LOW); 
    delay(2000);          
    }        
}

  if(mode == 0){
    lcd.setCursor(1,0);
    lcd.print("Enter Password");
    
 //      lcd.setCursor(1,1);
 //   lcd.print(FistTimePassword);
    
    
  }else if(mode == 1){
    lcd.setCursor(0,0);
    lcd.print("Set New Password");    
  }else if(mode == 2){
    lcd.setCursor(0,0);
    lcd.print("Password Again");      
  }else if(mode == 3){
    lcd.setCursor(4,0);
    lcd.print("UNLOCKED");         
  }


  if (key && key != '#' && mode != 3) 
  {
    collectKey();
  }

  if(data_count == Password_Lenght-1) 
  {
    if(mode == 0){
      lcd.clear();
      if(!strcmp(Data, Master)) {
        lcd.setCursor(2, 0);
        lcd.print("WELCOME BACK");
        lcd.setCursor(4, 1);
        lcd.print("MASTER");
        
        just_allowed_pass = 1;
        time_old = millis();
  
        digitalWrite(13, HIGH);
        
        delay(2000);
        mode = 3;
      }else{
        lcd.setCursor(2, 0);
        lcd.print("INCORRECT !");
        lcd.setCursor(4, 1);
        lcd.print("PASSWORD");
        delay(2000);
      }
      delay(1000);// 
      lcd.clear();
      clearData(); 
      
     // digitalWrite(13, LOW); 
    }else if( mode == 1){
      lcd.clear();
      mode = 2;
      for(int i = 0; i < Password_Lenght; i = i+1){
      Data2[i] = Data[i];
     }
      clearData(); 
    }else if(mode == 2){
      if(!strcmp(Data, Data2)){
        lcd.clear();
        lcd.setCursor(0, 0); 
        lcd.print("New Password is ");  
        lcd.setCursor(4, 1);   
        lcd.print(Data);  
        delay(2000);
        lcd.clear();
        lcd.setCursor(4, 0);
        lcd.print("Saving...");
        for(int i =0; i <= 100; i =  i+10){
          lcd.setCursor(4, 1);
          lcd.print(i);
          lcd.setCursor(7, 1);
          lcd.print("%");
          delay(200);
        }
        EEPROM.put(0, Data);
        EEPROM.get(0, Master);
        delay(500);
      }else{
        lcd.clear();
        lcd.setCursor(4, 0); 
        lcd.print("PASSWORD");  
        lcd.setCursor(3, 1);   
        lcd.print("NOT MATCH!");  
        delay(2000);        
      }
      mode = 3;
      clearData();
      lcd.clear();
    }
  }
}

void collectKey(){
  Data[data_count] = key; 
  lcd.setCursor(4+data_count,1); 
  lcd.print("*"); 
  data_count++;   
}

void clearData()
{
  while(data_count !=0)
  {  
    Data[data_count--] = 0; 
  }
}


void Check_EEPROM(){
  EEPROM.get(0, Master);
  if(Master[0] == 0 && Master[1] == 0 && Master[2] == 0 && Master[3] == 0){ // check if EEPRM have store password ?
    Serial.println("No EEPROM PASSWORD FOUND"); // if not found will burn EEPROM a first time password
    EEPROM.put(0, FistTimePassword);
    EEPROM.get(0, Master);
  }
}
